# Fritzing sketch ptr_2 (saved by Fritzing 0.9.4)
breadboards: 1

parts:
  ard_uno = Arduino Ethernet Shield (Rev3)
  D1(Orange) = Rectifier Diode [part_number=D0 package="300 mil [THT]"]
  C1815 = NPN-Transistor [package="TO92 [THT]"]
  L1 = Solenoid
  J1 = Power Jack [package=power_jack_slot]
  D1(Orange)1 = Rectifier Diode [part_number=D1 package="300 mil [THT]"]
  C1816 = NPN-Transistor [package="TO92 [THT]"]
  L2 = Solenoid
  TLP(P521) = TLP621 [package=THT]
  DIN1 = DIN-5 jack (MIDI) [package=THT]
  R1 = Resistor [tolerance=±5% resistance=220 package=THT]
  R2 = Resistor [tolerance=±5% resistance=1k package=THT]
  デュアル・モータードライバTB6612FNG = Motor Driver 1A Dual TB6612FNG
  MotorFader1 = DC Motor
  MotorFader2 = DC Motor
  Motor_fader_R1 = Slide Potentiometer [maximum_resistance=100kΩ]
  Motor_fader_R2 = Slide Potentiometer [maximum_resistance=100kΩ]
  L3 = Solenoid
  D1(Orange)2 = Rectifier Diode [part_number=D1 package="300 mil [THT]"]
  C1817 = NPN-Transistor [package="TO92 [THT]"]
  Water_surface = Pushbutton [package="[THT]"]

nets (from the breadboard view):
  5V: ard_uno.5V, R2.Pin_1, デュアル・モータードライバTB6612FNG.VCC, Motor_fader_R1.leg1, Motor_fader_R2.leg1
  N1: ard_uno.D8, デュアル・モータードライバTB6612FNG.BIN2
  N2: ard_uno.PWM_D9, デュアル・モータードライバTB6612FNG.STBY
  N3: ard_uno.PWM_D11, C1815.C
  N4: ard_uno.SPI/D12, C1816.C
  N5: ard_uno.SPI/D13, C1817.C
  GND: ard_uno.GND, C1815.E, J1.GND, C1816.E, TLP(P521).Pin_3, DIN1.2, デュアル・モータードライバTB6612FNG.GND, Motor_fader_R1.leg2, Motor_fader_R2.leg2, C1817.E, Water_surface.Pin_1, Water_surface.Pin_2
  N6: ard_uno.A0, Motor_fader_R1.wiper
  N7: ard_uno.A1, Motor_fader_R2.wiper
  N8: ard_uno.RX/D0, TLP(P521).Pin_4, R2.Pin_0
  N9: ard_uno.D2, Water_surface.Pin_3, Water_surface.Pin_4
  N10: ard_uno.PWM_D3, デュアル・モータードライバTB6612FNG.AIN1
  N11: ard_uno.SDCS, デュアル・モータードライバTB6612FNG.AIN2
  N12: ard_uno.PWM_D5, デュアル・モータードライバTB6612FNG.PWMA
  N13: ard_uno.PWM_D6, デュアル・モータードライバTB6612FNG.PWMB
  N14: ard_uno.D7, デュアル・モータードライバTB6612FNG.BIN1
  N15: D1(Orange).cathode, L1.pin2, J1.PWR, D1(Orange)1.cathode, L2.pin2, デュアル・モータードライバTB6612FNG.VM, L3.pin2, D1(Orange)2.cathode
  N16: D1(Orange).anode, C1815.B, L1.pin1
  N17: D1(Orange)1.anode, C1816.B, L2.pin1
  N18: TLP(P521).Pin_1, R1.Pin_0
  N19: TLP(P521).Pin_2, DIN1.5
  N20: DIN1.4, R1.Pin_1
  N21: デュアル・モータードライバTB6612FNG.B01, MotorFader2.pin_1
  N22: デュアル・モータードライバTB6612FNG.B02, MotorFader2.pin_2
  N23: デュアル・モータードライバTB6612FNG.A02, MotorFader1.pin_2
  N24: デュアル・モータードライバTB6612FNG.A01, MotorFader1.pin_1
  N25: L3.pin1, D1(Orange)2.anode, C1817.B
